# Fritzing sketch Fan (saved by Fritzing 1.0.5)
breadboards: 1

parts:
  D1 = Rectifier Diode [part_number=1N4007 package="300 mil [THT]"]
  F1 = Fan - Ventilador [package=THT]
  R1 = Resistor [tolerance=±5% power=0.25W resistance=330 package=THT]
  Q1 = NPN-Transistor [part_number=2N2222 package="TO92 [THT]"]
  R2 = Resistor [tolerance=±5% power=0.25W resistance=100k package=THT]
  M1 = DOIT Esp32 DevKit v1 (30 pins long, 11 pins width) [part_number=ESP32S-30Pin]

nets:
  5V: D1.cathode, F1.5V, M1.VIN
  N1: D1.anode, F1.GND, Q1.C
  N2: R1.Pin_0, Q1.B, R2.Pin_0
  N3: R1.Pin_1, M1.D25
  N4: Q1.E, R2.Pin_1, M1.GND

custom parts:
  Fan - Ventilador: Ventilador de 2 pines, se encuentra comunmente en computadoras de escritorio
  DOIT Esp32 DevKit v1 (30 pins long, 11 pins width): The DOIT Esp32 DevKit v1 is one of the development board created by DOIT to evaluate the ESP-WROOM-32 module. It is based on the ESP32 microcontroller that boasts Wifi, Bluetooth, Ethernet and Low Power support all in a single chip. (vanepp) made breadboard work, adjusted pin numbering and labels and reduced size of schematic and cleaned up pcb. This chip is 30pins long (2 x15) and 11 pins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
