# Fritzing sketch WiringDiagram (saved by Fritzing 1.0.5)

parts:
  M2 = DOIT Esp32 DevKit v1 (30 pins long, 11 pins width) [part_number=ESP32S-PIN30]
  From_JK_485_converter = Header 4 [package=screwterminal-3.5mm-4_lock]
  M3 = MAX485 Breakout [package=THT]

nets:
  3V3: M2.3V3, M3.VCC
  GND: M2.GND, From_JK_485_converter.RS485_Gnd_(Black), M3.GND
  N1: M2.RX2, M3.RO
  N2: M2.TX2, M3.DI
  N3: From_JK_485_converter.RS485_A_(yellow), M3.A
  N4: From_JK_485_converter.RS485_B_(White), M3.B

custom parts:
  DOIT Esp32 DevKit v1 (30 pins long, 11 pins width): The DOIT Esp32 DevKit v1 is one of the development board created by DOIT to evaluate the ESP-WROOM-32 module. It is based on the ESP32 microcontroller that boasts Wifi, Bluetooth, Ethernet and Low Power support all in a single chip. (vanepp) made breadboard work, adjusted pin numbering and labels and reduced size of schematic and cleaned up pcb. This chip is 30pins long (2 x15) and 11 pins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
  Header 4: Header 4 Standard 4-pin 0.1 header. Use with straight break away headers (SKU : PRT-00116), right angle break away headers (PRT-00553), swiss pins (PRT-00743), machine pins (PRT-00117), and female headers (PRT-00115). Molex polarized connector foot print use with SKU : PRT-08231 with associated crimp pins and housings. 1MM SMD Version SKU: PRT-10208
  MAX485 Breakout: MAX485 RS485 breakout board
